// Logisim project ControlUnit.circ as structural Verilog: 1 circuit, main circuit ControlUnit
module ControlUnit (
  input  [5:0] Opcode,
  input  [5:0] Func,
  output ALUSrc,
  output RegWrite,
  output [5:0] ALUOp,
  output ALUOpValid,
  output [3:0] MemMask,
  output JAL,
  output JumpReg,
  output RegDest,
  output Jump,
  output Branch,
  output LB,
  output MemToReg,
  output Syscall,
  output SLTi
);

  wire and_1_out, and_2_out, and_3_out, and_4_out, and_6_out, and_7_out, and_9_out, and_10_out, and_13_out,
       and_15_out, and_16_out, and_17_out, and_18_out, and_19_out, and_20_out, and_21_out, fu0not, fu1not,
       fu2not, fu3not, fu4not, fu5not, J, nand_1_out, nand_2_out, nor_2_out, not_13_out, not_14_out,
       not_15_out, op0not, op1not, op2not, op3not, op4not, op5not, or_1_out, or_2_out, or_4_out, or_5_out,
       or_6_out, or_7_out;

  and and_1 (and_1_out, op5not, Opcode[1], op3not);
  not not_1 (op5not, Opcode[0]);
  not not_2 (fu5not, Func[0]);
  and and_2 (and_2_out, op0not, op1not, op2not, op3not, Opcode[1], Opcode[0]);
  and and_3 (and_3_out, op4not, op3not);
  and and_4 (and_4_out, op0not, op1not, Opcode[3]);
  or or_1 (or_1_out, Opcode[2], and_3_out, and_1_out);
  not not_3 (op4not, Opcode[1]);
  not not_4 (op3not, Opcode[2]);
  not not_5 (op2not, Opcode[3]);
  not not_6 (op1not, Opcode[4]);
  not not_7 (op0not, Opcode[5]);
  not not_8 (fu4not, Func[1]);
  not not_9 (fu3not, Func[2]);
  not not_10 (fu2not, Func[3]);
  not not_11 (fu1not, Func[4]);
  not not_12 (fu0not, Func[5]);
  and and_5 (LB, Opcode[5], op1not, op2not, op3not, op4not, op5not);
  nand nand_1 (nand_1_out, fu0not, fu1not, Func[3], fu3not, fu4not, fu5not);
  and and_6 (and_6_out, and_4_out, or_1_out);
  and and_7 (and_7_out, RegDest, nand_1_out);
  or or_2 (or_2_out, and_2_out, MemToReg, and_6_out);
  or or_3 (RegWrite, and_7_out, or_2_out);
  and and_8 (JumpReg, fu0not, fu1not, Func[3], fu3not, fu4not, fu5not);
  nor nor_1 (RegDest, Opcode[5], Opcode[4], Opcode[3], Opcode[2], Opcode[1], Opcode[0]);
  not not_13 (not_13_out, RegDest);
  and and_9 (and_9_out, Opcode[1], Opcode[0]);
  and and_10 (and_10_out, op4not, op5not);
  and and_11 (JAL, op0not, op1not, op2not, op3not, Opcode[1], Opcode[0]);
  and and_12 (Syscall, fu0not, fu1not, Func[3], Func[2], fu4not, fu5not);
  not not_14 (not_14_out, Branch);
  or or_4 (or_4_out, and_9_out, and_10_out);
  and and_13 (and_13_out, op0not, op1not, Opcode[3], Opcode[2], Opcode[1], Opcode[0]);
  and and_14 (ALUSrc, not_13_out, not_14_out);
  and and_15 (and_15_out, op3not, op1not, Opcode[5], or_4_out);
  or or_5 (or_5_out, J, and_13_out);
  and and_16 (and_16_out, Opcode[1], Opcode[0]);
  and and_17 (and_17_out, op4not, op5not);
  nand nand_2 (nand_2_out, fu0not, fu1not, Func[3], fu4not, fu5not);
  not not_15 (not_15_out, RegDest);
  nor nor_2 (nor_2_out, and_15_out, or_5_out);
  and and_18 (and_18_out, op3not, op4not, Opcode[0]);
  or or_6 (or_6_out, and_16_out, and_17_out);
  and and_19 (and_19_out, RegDest, nand_2_out);
  and and_20 (and_20_out, not_15_out, nor_2_out);
  and and_21 (and_21_out, op0not, op1not, Opcode[3], Opcode[2], Opcode[1], Opcode[0]);
  and and_22 (J, op0not, op1not, op2not, op3not, Opcode[1]);
  or or_7 (or_7_out, Opcode[2], and_18_out);
  and and_23 (MemToReg, Opcode[5], op1not, op3not, op2not, or_6_out);
  and and_24 (MemMask[3], or_6_out, Opcode[5], op1not, Opcode[3], op3not);
  or or_8 (ALUOpValid, and_19_out, and_20_out, and_21_out);
  or or_9 (Jump, JumpReg, J);
  and and_25 (Branch, op0not, op1not, op2not, or_7_out);
  and and_26 (MemMask[2], Opcode[5], op1not, Opcode[3], op3not, Opcode[1], Opcode[0]);
  and and_27 (SLTi, op0not, op1not, Opcode[3], op3not, Opcode[1], op5not);

  assign ALUOp = Opcode;
  assign MemMask[1:0] = {2{MemMask[2]}};

  // Other names for the same wires on the sheet: fu5 = Func[0]; fu4 = Func[1]; fu3 = Func[2]; fu2 = Func[3];
  //   fu1 = Func[4]; fu0 = Func[5]; op5 = Opcode[0]; op4 = Opcode[1]; op3 = Opcode[2]; op2 = Opcode[3];
  //   op1 = Opcode[4]; op0 = Opcode[5]

  // Notes on the sheet:
  //   Control Unit inputs
  //   Control Unit outputs
endmodule
