// Logisim project DFF_FiveBit.circ as structural Verilog: 1 circuit, main circuit DFF_FiveBit
module DFF_FiveBit (
  input  [4:0] in_1,
  input  in_2,
  output [4:0] out_3
);

  D_Flip_Flop d_ff_1 (.D(in_1[0]), .clk(in_2), .Q(out_3[0]));  // open: Qn, preset, reset
  D_Flip_Flop d_ff_2 (.D(in_1[1]), .clk(in_2), .Q(out_3[1]));  // open: Qn, preset, reset
  D_Flip_Flop d_ff_3 (.D(in_1[2]), .clk(in_2), .Q(out_3[2]));  // open: Qn, preset, reset
  D_Flip_Flop d_ff_4 (.D(in_1[3]), .clk(in_2), .Q(out_3[3]));  // open: Qn, preset, reset
  D_Flip_Flop d_ff_5 (.D(in_1[4]), .clk(in_2), .Q(out_3[4]));  // open: Qn, preset, reset
endmodule
