// Logisim project EX_MEM_buffer.circ as structural Verilog: 1 circuit, main circuit EX_MEM
module EX_MEM (
  input  clk,
  input  [31:0] PC,
  input  [31:0] Result,
  input  [31:0] RD2,
  input  [4:0] Write,
  input  Zero,
  input  Branch,
  input  [3:0] MemMask,
  input  MemToReg,
  input  JAL,
  input  RegWrite,
  input  [31:0] added_PC,
  input  reset,
  output [31:0] n_Result,
  output [31:0] n_PC,
  output [31:0] n_RD2,
  output [4:0] n_Write,
  output n_Zero,
  output n_Branch,
  output [3:0] n_MemMask,
  output n_MemToReg,
  output n_JAL,
  output n_RegWrite,
  output [31:0] n_added_PC
);

  Register #(.width(32)) register_1 (.D(PC), .en(1'b1), .clk(clk), .Q(n_PC), .clr(reset));
  Register #(.width(32)) register_2 (.D(Result), .en(1'b1), .clk(clk), .Q(n_Result), .clr(reset));
  Register #(.width(32)) register_3 (.D(RD2), .en(1'b1), .clk(clk), .Q(n_RD2), .clr(reset));
  Register #(.width(1)) register_4 (.D(Zero), .en(1'b1), .clk(clk), .Q(n_Zero), .clr(reset));
  Register #(.width(5)) register_5 (.D(Write), .en(1'b1), .clk(clk), .Q(n_Write), .clr(reset));
  Register #(.width(1)) register_6 (.D(Branch), .en(1'b1), .clk(clk), .Q(n_Branch), .clr(reset));
  Register #(.width(1)) register_7 (.D(MemToReg), .en(1'b1), .clk(clk), .Q(n_MemToReg), .clr(reset));
  Register #(.width(32)) register_8 (.D(added_PC), .en(1'b1), .clk(clk), .Q(n_added_PC), .clr(reset));
  Register #(.width(1)) register_9 (.D(JAL), .en(1'b1), .clk(clk), .Q(n_JAL), .clr(reset));
  Register #(.width(4)) register_10 (.D(MemMask), .en(1'b1), .clk(clk), .Q(n_MemMask), .clr(reset));
  Register #(.width(1)) register_11 (.D(RegWrite), .en(1'b1), .clk(clk), .Q(n_RegWrite), .clr(reset));

  // Notes on the sheet:
  //   inputs
  //   outputs
endmodule
