// Logisim project Forward.circ as structural Verilog: 1 circuit, main circuit Forward
module Forward (
  input  [4:0] WriteReg,
  input  [4:0] ReadRegI,
  input  [4:0] ReadRegII,
  input  clk,
  input  [31:0] ALUResult,
  input  [31:0] MEMResult,
  input  [31:0] SignalI,
  input  [31:0] SignalII,
  output [31:0] outI,
  output [31:0] outII
);

  wire and_1_out, and_2_out, comparator_1_eq, comparator_2_eq, comparator_3_eq, comparator_4_eq, d_ff_1_q,
       NOP, not_1_out, not_2_out, or_1_out, or_2_out, or_3_out;
  wire [1:0] SI, SII;
  wire [4:0] dff_fivebit_1_out_3, dff_fivebit_2_out_3;

  Multiplexer #(.select(2), .width(32)) multiplexer_1 (
    .in0(SignalI), .in1(ALUResult), .in2(MEMResult), .in3(ALUResult), .out(outI), .sel(SI));
  DFF_FiveBit dff_fivebit_1 (.in_1(WriteReg), .in_2(clk), .out_3(dff_fivebit_1_out_3));
  Multiplexer #(.select(2), .width(32)) multiplexer_2 (
    .in0(SignalII), .in1(ALUResult), .in2(MEMResult), .in3(ALUResult), .out(outII), .sel(SII));
  Comparator #(.width(5)) comparator_1 (.a(dff_fivebit_1_out_3), .b(ReadRegI), .eq(comparator_1_eq));  // open: gt, lt
  Comparator #(.width(5)) comparator_2 (.a(dff_fivebit_1_out_3), .b(ReadRegII), .eq(comparator_2_eq));  // open: gt, lt
  Comparator #(.width(5)) comparator_3 (.a(dff_fivebit_2_out_3), .b(ReadRegI), .eq(comparator_3_eq));  // open: gt, lt
  Comparator #(.width(5)) comparator_4 (.a(dff_fivebit_2_out_3), .b(ReadRegII), .eq(comparator_4_eq));  // open: gt, lt
  Comparator #(.width(5)) comparator_5 (.a(WriteReg), .b({5{1'b0}}), .eq(NOP));  // open: gt, lt
  DFF_FiveBit dff_fivebit_2 (.in_1(dff_fivebit_1_out_3), .in_2(clk), .out_3(dff_fivebit_2_out_3));
  or or_1 (or_1_out, comparator_1_eq, comparator_2_eq);
  or or_2 (or_2_out, comparator_3_eq, comparator_4_eq);
  not not_1 (not_1_out, NOP);
  not not_2 (not_2_out, NOP);
  and and_1 (and_1_out, or_2_out, not_1_out);
  and and_2 (and_2_out, or_1_out, not_2_out);
  and and_3 (SI[0], comparator_3_eq, and_1_out);
  D_Flip_Flop d_ff_1 (.D(and_2_out), .clk(clk), .Q(d_ff_1_q));  // open: Qn, preset, reset
  or or_3 (or_3_out, and_2_out, d_ff_1_q);
  and and_4 (SI[1], comparator_1_eq, or_3_out);
  and and_5 (SII[1], or_3_out, comparator_2_eq);
  and and_6 (SII[0], and_1_out, comparator_4_eq);
endmodule
