// Logisim project MEM_WB_buffer.circ as structural Verilog: 1 circuit, main circuit MEM_WB
module MEM_WB (
  input  clk,
  input  [31:0] PC,
  input  [31:0] Result,
  input  [31:0] Data,
  input  [4:0] Write,
  input  MemToReg,
  input  JAL,
  input  RegWrite,
  input  reset,
  output [31:0] n_Result,
  output [31:0] n_PC,
  output [31:0] n_Data,
  output [4:0] n_Write,
  output n_MemToReg,
  output n_JAL,
  output n_RegWrite
);

  Register #(.width(32)) register_1 (.D(PC), .en(1'b1), .clk(clk), .Q(n_PC), .clr(reset));
  Register #(.width(32)) register_2 (.D(Result), .en(1'b1), .clk(clk), .Q(n_Result), .clr(reset));
  Register #(.width(32)) register_3 (.D(Data), .en(1'b1), .clk(clk), .Q(n_Data), .clr(reset));
  Register #(.width(5)) register_4 (.D(Write), .en(1'b1), .clk(clk), .Q(n_Write), .clr(reset));
  Register #(.width(1)) register_5 (.D(MemToReg), .en(1'b1), .clk(clk), .Q(n_MemToReg), .clr(reset));
  Register #(.width(1)) register_6 (.D(JAL), .en(1'b1), .clk(clk), .Q(n_JAL), .clr(reset));
  Register #(.width(1)) register_7 (.D(RegWrite), .en(1'b1), .clk(clk), .Q(n_RegWrite), .clr(reset));

  // Notes on the sheet:
  //   inputs
  //   outputs
endmodule
