// Logisim project MemAddressGen.circ as structural Verilog: 1 circuit, main circuit MemAddressGen
module MemAddressGen (
  input  [13:0] address,
  input  miss,
  input  clk,
  input  read,
  output [3:0] memmask,
  output [13:0] memaddress,
  output readmem
);

  wire and_1_out, and_2_out, and_3_out, and_4_out, nand_1_out, not_1_out, not_2_out, not_3_out, or_1_out,
       t_ff_1_qn;

  not not_1 (not_1_out, read);
  and and_1 (and_1_out, read, not_1_out);
  nand nand_1 (nand_1_out, memaddress[0], memaddress[1]);
  and and_2 (and_2_out, and_1_out, t_ff_1_qn);
  not not_2 (not_2_out, and_1_out);
  and and_3 (and_3_out, clk, nand_1_out);
  T_Flip_Flop t_ff_1 (.T(not_2_out), .clk(and_3_out), .Q(memaddress[0]), .Qn(t_ff_1_qn));  // open: reset, preset
  and and_4 (and_4_out, not_2_out, memaddress[0]);
  or or_1 (or_1_out, and_4_out, and_2_out);
  T_Flip_Flop t_ff_2 (.T(or_1_out), .clk(and_3_out), .Q(memaddress[1]));  // open: Qn, reset, preset
  not not_3 (not_3_out, read);
  or or_2 (memmask[3], read, not_3_out);

  assign memaddress[13:2] = address[13:2];
  assign memmask[2:0] = {3{memmask[3]}};
  assign readmem = read;

  // Other names for the same wires on the sheet: bit0 = memaddress[0]; bit1 = memaddress[1];
  //   address_t[11:0] = address[13:2]

  // Notes on the sheet:
  //   Inputs
  //   output
endmodule
