// Logisim project PipelineFlush.circ as structural Verilog: 1 circuit, main circuit PipelineFlush
module PipelineFlush (
  input  [4:0] WriteReg,
  input  [4:0] ReadRegI,
  input  [4:0] ReadRegII,
  input  Branch,
  input  BranchPrediction,
  input  BranchResult,
  input  clk,
  input  MemToReg,
  output RAWFlush,
  output BranchFlush,
  output LoadFlush
);

  wire and_3_out, and_4_out, comparator_1_eq, comparator_2_eq, comparator_3_eq, comparator_4_eq,
       comparator_6_eq, comparator_7_eq, d_ff_1_q, d_ff_2_q, d_ff_3_q, d_ff_4_q, d_ff_6_q, Load, NOP,
       not_1_out, not_2_out, not_3_out, OneStall, or_1_out, or_2_out, or_4_out, TwoStall, xor_1_out;
  wire [4:0] dff_fivebit_1_out_3, dff_fivebit_2_out_3, dff_fivebit_3_out_3;

  D_Flip_Flop d_ff_1 (.D(BranchPrediction), .clk(clk), .Q(d_ff_1_q));  // open: Qn, preset, reset
  D_Flip_Flop d_ff_2 (.D(MemToReg), .clk(clk), .Q(d_ff_2_q));  // open: Qn, preset, reset
  xor xor_1 (xor_1_out, BranchResult, d_ff_3_q);
  D_Flip_Flop d_ff_3 (.D(d_ff_1_q), .clk(clk), .Q(d_ff_3_q));  // open: Qn, preset, reset
  D_Flip_Flop d_ff_4 (.D(d_ff_2_q), .clk(clk), .Q(d_ff_4_q));  // open: Qn, preset, reset
  and and_1 (BranchFlush, Branch, xor_1_out);
  D_Flip_Flop d_ff_5 (.D(d_ff_4_q), .clk(clk), .Q(Load));  // open: Qn, preset, reset
  DFF_FiveBit dff_fivebit_1 (.in_1(WriteReg), .in_2(clk), .out_3(dff_fivebit_1_out_3));
  Comparator #(.width(5)) comparator_1 (.a(dff_fivebit_1_out_3), .b(ReadRegI), .eq(comparator_1_eq));  // open: gt, lt
  Comparator #(.width(5)) comparator_2 (.a(dff_fivebit_1_out_3), .b(ReadRegII), .eq(comparator_2_eq));  // open: gt, lt
  Comparator #(.width(5)) comparator_3 (.a(dff_fivebit_2_out_3), .b(ReadRegI), .eq(comparator_3_eq));  // open: gt, lt
  Comparator #(.width(5)) comparator_4 (.a(dff_fivebit_2_out_3), .b(ReadRegII), .eq(comparator_4_eq));  // open: gt, lt
  Comparator #(.width(5)) comparator_5 (.a(WriteReg), .b({5{1'b0}}), .eq(NOP));  // open: gt, lt
  Multiplexer multiplexer_1 (.in0(OneStall), .in1(TwoStall), .out(RAWFlush), .sel(TwoStall));
  DFF_FiveBit dff_fivebit_2 (.in_1(dff_fivebit_1_out_3), .in_2(clk), .out_3(dff_fivebit_2_out_3));
  or or_1 (or_1_out, comparator_1_eq, comparator_2_eq);
  or or_2 (or_2_out, comparator_3_eq, comparator_4_eq);
  not not_1 (not_1_out, NOP);
  DFF_FiveBit dff_fivebit_3 (.in_1(dff_fivebit_2_out_3), .in_2(clk), .out_3(dff_fivebit_3_out_3));
  not not_2 (not_2_out, NOP);
  and and_2 (OneStall, or_2_out, not_1_out);
  and and_3 (and_3_out, or_1_out, not_2_out);
  Comparator #(.width(5)) comparator_6 (.a(dff_fivebit_3_out_3), .b(ReadRegI), .eq(comparator_6_eq));  // open: gt, lt
  Comparator #(.width(5)) comparator_7 (.a(dff_fivebit_3_out_3), .b(ReadRegII), .eq(comparator_7_eq));  // open: gt, lt
  D_Flip_Flop d_ff_6 (.D(and_3_out), .clk(clk), .Q(d_ff_6_q));  // open: Qn, preset, reset
  or or_3 (TwoStall, and_3_out, d_ff_6_q);
  or or_4 (or_4_out, comparator_6_eq, comparator_7_eq);
  and and_4 (and_4_out, or_4_out, not_3_out);
  not not_3 (not_3_out, NOP);
  and and_5 (LoadFlush, and_4_out, Load);
endmodule
