// Logisim project SaturatingCounter_2bit.circ as structural Verilog: 1 circuit, main circuit SaturatingCounter_2bit
module SaturatingCounter_2bit (
  input  request,
  input  result,
  input  teken,
  input  clk,
  output prediction
);

  wire comparator_1_gt, comparator_2_lt, countMSB, multiplexer_5_out;
  wire [0:0] multiplexer_4_out;
  wire [1:0] adder_1_out, count, multiplexer_1_out, multiplexer_2_out, multiplexer_3_out, subtractor_1_out;

  D_Flip_Flop d_ff_1 (.D(multiplexer_4_out[0]), .clk(clk), .Q(count[0]));  // open: Qn, preset, reset
  D_Flip_Flop d_ff_2 (.D(countMSB), .clk(clk), .Q(count[1]));  // open: Qn, preset, reset
  Comparator #(.mode("unsigned"), .width(2)) comparator_1 (.a(count), .b(2'b00), .gt(comparator_1_gt));  // open: eq, lt
  Subtractor #(.width(2)) subtractor_1 (.a(count), .b(2'b01), .out(subtractor_1_out));  // open: bin, bout
  Comparator #(.mode("unsigned"), .width(2)) comparator_2 (.a(count), .b(2'b11), .lt(comparator_2_lt));  // open: gt, eq
  Adder #(.width(2)) adder_1 (.a(count), .b(2'b01), .out(adder_1_out));  // open: cin, cout
  Multiplexer #(.width(2)) multiplexer_1 (
    .in0(count), .in1(subtractor_1_out), .out(multiplexer_1_out), .sel(comparator_1_gt));
  Multiplexer #(.width(2)) multiplexer_2 (
    .in0(count), .in1(adder_1_out), .out(multiplexer_2_out), .sel(comparator_2_lt));
  Multiplexer #(.width(2)) multiplexer_3 (
    .in0(multiplexer_1_out), .in1(multiplexer_2_out), .out(multiplexer_3_out), .sel(teken));
  Multiplexer #(.width(2)) multiplexer_4 (
    .in0(count), .in1(multiplexer_3_out), .out({countMSB, multiplexer_4_out[0]}), .sel(result));
  D_Flip_Flop d_ff_3 (.D(multiplexer_5_out), .clk(clk), .Q(prediction));  // open: Qn, preset, reset
  Multiplexer multiplexer_5 (.in0(prediction), .in1(countMSB), .out(multiplexer_5_out), .sel(request));

  // Other names for the same wires on the sheet: taken = teken
endmodule
