// Logisim project alu_control.circ as structural Verilog: 1 circuit, main circuit aluControl
module aluControl (
  input  [5:0] func,
  input  [6:0] aluOP,
  output [5:0] opcd_fnc,
  output is_op
);

  Multiplexer #(.width(6)) multiplexer_1 (.in0(func), .in1(aluOP[5:0]), .out(opcd_fnc), .sel(is_op));
  or or_1 (is_op, aluOP[0], aluOP[1], aluOP[2], aluOP[3], aluOP[4], aluOP[5]);

  // Other names for the same wires on the sheet: isopc = is_op

  // Notes on the sheet:
  //   inputs
  //   outputs
  //   logic
endmodule
