// Logisim project alu_final.circ as structural Verilog: 1 circuit, main circuit alu
module alu (
  input  [31:0] rs,
  input  [31:0] rt_imm,
  input  [5:0] opcd_fnc,
  input  [4:0] shft_amt,
  input  is_i,
  output [31:0] result,
  output zero
);

  wire c_i1, c_i2, c_i3, c_i4, c_i5, c_i6, c_i7, c_i8, c_i9, c_i10, c_i11, c_i12, c_i13, c_i14, c_i15, c_i16,
       c_r1, c_r2, c_r3, c_r4, c_r5, c_r6, c_r7, c_r8, c_r9, c_r10, c_r11, c_r12, c_r13, c_r14, c_r15, c_r16,
       c_r17, c_r18, comparator_1_eq, comparator_1_gt, comparator_1_lt, comparator_2_eq, comparator_2_gt,
       comparator_2_lt, f0p, f1p, f2p, f3p, f4p, f5p, not_7_out, or_1_out, or_2_out, or_4_out,
       priority_encoder_1_en_out;
  wire [4:0] i_ins, r_ins;
  wire [31:0] c_add, c_and, c_bez, c_big, c_bz, c_cmp, c_div, c_equ, c_lez, c_mul, c_neq, c_nor, c_or,
       c_shft10, c_sll, c_sllv, c_sra, c_srl, c_srlv, c_sub, c_unk, c_xor, i_output, r_output;

  not not_1 (f0p, opcd_fnc[0]);
  not not_2 (f1p, opcd_fnc[1]);
  not not_3 (f2p, opcd_fnc[2]);
  not not_4 (f3p, opcd_fnc[3]);
  not not_5 (f4p, opcd_fnc[4]);
  not not_6 (f5p, opcd_fnc[5]);
  and and_1 (c_r1, f0p, opcd_fnc[1], opcd_fnc[2], f3p, f4p, opcd_fnc[5]);
  and and_2 (c_r2, f0p, f1p, f2p, f3p, f4p, f5p);
  and and_3 (c_r3, f0p, f1p, opcd_fnc[2], f3p, f4p, f5p);
  and and_4 (c_r4, f0p, opcd_fnc[1], f2p, f3p, f4p, f5p);
  and and_5 (c_r5, f0p, opcd_fnc[1], f2p, f3p, f4p, opcd_fnc[5]);
  and and_6 (c_r6, f0p, opcd_fnc[1], opcd_fnc[2], f3p, f4p, f5p);
  and and_7 (c_r7, f0p, opcd_fnc[1], f2p, opcd_fnc[3], f4p, opcd_fnc[5]);
  and and_8 (c_r8, f0p, f1p, opcd_fnc[2], opcd_fnc[3], f4p, f5p);
  and and_9 (c_r9, opcd_fnc[0], opcd_fnc[1], f2p, f3p, f4p, opcd_fnc[5]);
  and and_10 (c_r10, opcd_fnc[0], f1p, opcd_fnc[2], f3p, f4p, opcd_fnc[5]);
  and and_11 (c_r11, opcd_fnc[0], opcd_fnc[1], opcd_fnc[2], f3p, f4p, opcd_fnc[5]);
  and and_12 (c_r12, opcd_fnc[0], f1p, f2p, f3p, f4p, opcd_fnc[5]);
  and and_13 (c_i1, f0p, f1p, f2p, opcd_fnc[3], f4p, f5p);
  and and_14 (c_i2, opcd_fnc[0], f1p, f2p, opcd_fnc[3], f4p, f5p);
  and and_15 (c_r13, f0p, f1p, f2p, opcd_fnc[3], opcd_fnc[4], f5p);
  and and_16 (c_r14, f0p, opcd_fnc[1], f2p, opcd_fnc[3], opcd_fnc[4], f5p);
  and and_17 (c_r15, f0p, f1p, opcd_fnc[2], f3p, f4p, opcd_fnc[5]);
  and and_18 (c_r16, f0p, f1p, f2p, f3p, f4p, opcd_fnc[5]);
  and and_19 (c_r17, f0p, f1p, f2p, opcd_fnc[3], f4p, f5p);
  and and_20 (c_r18, opcd_fnc[0], opcd_fnc[1], f2p, f3p, f4p, f5p);
  and and_21 (c_i3, f0p, f1p, opcd_fnc[2], opcd_fnc[3], f4p, f5p);
  and and_22 (c_i4, f0p, opcd_fnc[1], opcd_fnc[2], opcd_fnc[3], f4p, f5p);
  Comparator #(.width(32)) comparator_1 (
    .a(rs), .b(rt_imm), .gt(comparator_1_gt), .eq(comparator_1_eq), .lt(comparator_1_lt));
  assign c_cmp = {{31{1'b0}}, comparator_1_lt};  // Bit_Extender bit_extender_1
  Comparator #(.width(32)) comparator_2 (
    .a(rs), .b({32{1'b0}}), .gt(comparator_2_gt), .eq(comparator_2_eq), .lt(comparator_2_lt));
  and and_23 (c_i5, opcd_fnc[0], f1p, opcd_fnc[2], opcd_fnc[3], f4p, f5p);
  and and_24 (c_i6, f0p, f1p, opcd_fnc[2], f3p, f4p, f5p);
  Subtractor #(.width(32)) subtractor_1 (.a(rs), .b(rt_imm), .out(c_sub));  // open: bin, bout
  Adder #(.width(32)) adder_1 (.a(rs), .b(rt_imm), .out(c_add));  // open: cin, cout
  Multiplier #(.width(32)) multiplier_1 (.a(rs), .b(rt_imm), .out(c_mul));  // open: cin, cout
  Divider #(.width(32)) divider_1 (.a(rs), .b(rt_imm), .out(c_div));  // open: upper, rem
  not not_7 (not_7_out, comparator_1_eq);
  or or_1 (or_1_out, comparator_2_gt, comparator_2_eq);
  or or_2 (or_2_out, comparator_2_eq, comparator_2_lt);
  assign c_xor = rs ^ rt_imm;  // XOR_Gate xor_1, 32 bits wide
  assign c_or = rs | rt_imm;  // OR_Gate or_3, 32 bits wide
  assign c_nor = ~(rs | rt_imm);  // NOR_Gate nor_1, 32 bits wide
  assign c_and = rs & rt_imm;  // AND_Gate and_25, 32 bits wide
  Shifter #(.width(32)) shifter_1 (.in(rt_imm), .\dist (shft_amt), .out(c_sll));
  Shifter #(.shift("lr"), .width(32)) shifter_2 (.in(rt_imm), .\dist (shft_amt), .out(c_srl));
  Shifter #(.width(32)) shifter_3 (.in(rt_imm), .\dist (rs[4:0]), .out(c_sllv));
  Shifter #(.shift("lr"), .width(32)) shifter_4 (.in(rt_imm), .\dist (rs[4:0]), .out(c_srlv));
  Shifter #(.shift("ar"), .width(32)) shifter_5 (.in(rt_imm), .\dist (shft_amt), .out(c_sra));
  Shifter #(.width(32)) shifter_6 (.in(rt_imm), .\dist (5'b10000), .out(c_shft10));
  assign c_big = {{31{1'b0}}, comparator_1_gt};  // Bit_Extender bit_extender_2
  assign c_equ = {{31{1'b0}}, comparator_1_eq};  // Bit_Extender bit_extender_3
  assign c_neq = {{31{1'b0}}, not_7_out};  // Bit_Extender bit_extender_4
  assign c_bz = {{31{1'b0}}, comparator_2_gt};  // Bit_Extender bit_extender_5
  assign c_bez = {{31{1'b0}}, or_1_out};  // Bit_Extender bit_extender_6
  assign c_lez = {{31{1'b0}}, or_2_out};  // Bit_Extender bit_extender_7
  and and_26 (c_i7, opcd_fnc[0], f1p, opcd_fnc[2], f3p, f4p, f5p);
  and and_27 (c_i8, f0p, opcd_fnc[1], opcd_fnc[2], f3p, f4p, f5p);
  and and_28 (c_i9, opcd_fnc[0], opcd_fnc[1], opcd_fnc[2], f3p, f4p, f5p);
  and and_29 (c_i10, opcd_fnc[0], f1p, f2p, f3p, f4p, f5p);
  Priority_Encoder #(.select(5)) priority_encoder_1 (
    .in0(1'b1), .in1(c_r1), .in2(c_r2), .in3(c_r3), .in4(c_r4), .in5(c_r5), .in6(c_r6), .in7(c_r7),
    .in8(c_r8), .in9(c_r9), .in10(c_r10), .in11(c_r11), .in12(c_r12), .in13(c_r13), .in14(c_r14),
    .in15(c_r15), .in16(c_r16), .in17(c_r17), .in18(c_r18), .out(r_ins), .en_out(priority_encoder_1_en_out),
    .en_in(1'b1));  // open: in19, in20, in21, in22, in23, in24, in25, in26, in27, in28, in29, in30, in31, gs
  Multiplexer #(.select(5), .width(32)) multiplexer_1 (
    .in1(c_xor), .in2(c_sll), .in3(c_sllv), .in4(c_srl), .in5(c_sub), .in6(c_srlv), .in7(c_cmp), .in8(c_unk),
    .in9(c_sub), .in10(c_or), .in11(c_nor), .in12(c_add), .in13(c_mul), .in14(c_div), .in15(c_and),
    .in16(c_add), .in17(rs), .in18(c_sra), .out(r_output), .sel(r_ins));  // open: in0, in19, in20, in21, in22, in23, in24, in25, in26, in27, in28, in29, in30, in31
  and and_30 (c_i11, opcd_fnc[0], opcd_fnc[1], f2p, f3p, f4p, opcd_fnc[5]);
  and and_31 (c_i12, opcd_fnc[0], opcd_fnc[1], f2p, opcd_fnc[3], f4p, opcd_fnc[5]);
  Multiplexer #(.width(32)) multiplexer_2 (.in0(r_output), .in1(i_output), .out(result), .sel(is_i));
  or or_4 (or_4_out, c_i6, c_i7, c_i8, c_i9, c_i10);
  Priority_Encoder #(.select(5)) priority_encoder_2 (
    .in0(1'b1), .in1(c_i1), .in2(c_i2), .in3(c_i3), .in4(c_i4), .in5(c_i5), .in6(c_i6), .in7(c_i7),
    .in8(c_i8), .in9(c_i9), .in10(c_i10), .in11(c_i11), .in12(c_i12), .in13(c_i13), .in14(c_i14),
    .in15(c_i15), .in16(c_i16), .out(i_ins), .en_in(1'b1));  // open: in17, in18, in19, in20, in21, in22, in23, in24, in25, in26, in27, in28, in29, in30, in31, gs, en_out
  and and_32 (zero, result[0], or_4_out);
  and and_33 (c_i13, f0p, f1p, f2p, f3p, f4p, opcd_fnc[5]);
  and and_34 (c_i14, f0p, f1p, f2p, opcd_fnc[3], f4p, opcd_fnc[5]);
  and and_35 (c_i15, f0p, opcd_fnc[1], f2p, opcd_fnc[3], f4p, f5p);
  and and_36 (c_i16, opcd_fnc[0], opcd_fnc[1], opcd_fnc[2], opcd_fnc[3], f4p, f5p);
  Multiplexer #(.select(5), .width(32)) multiplexer_3 (
    .in1(c_add), .in2(c_add), .in3(c_and), .in4(c_xor), .in5(c_or), .in6(c_equ), .in7(c_neq), .in8(c_lez),
    .in9(c_bz), .in10(c_bez), .in11(c_add), .in12(c_add), .in13(c_add), .in14(c_add), .in15(c_cmp),
    .in16(c_shft10), .out(i_output), .sel(i_ins));  // open: in0, in17, in18, in19, in20, in21, in22, in23, in24, in25, in26, in27, in28, in29, in30, in31

  // Other names for the same wires on the sheet: isopc = is_i; f0 = opcd_fnc[0]; op[5:0] = opcd_fnc; f1 = opcd_fnc[1];
  //   f2 = opcd_fnc[2]; f3 = opcd_fnc[3]; f4 = opcd_fnc[4]; f5 = opcd_fnc[5]; rt[31:0] = rt_imm;
  //   shamt[4:0] = shft_amt

  // Notes on the sheet:
  //   Input
  //   R Instructions Functions
  //   I instructions functions
  //   logical
  //   arithmetic
  //   R instructions
  //   I instructions
  //   Output
endmodule
