// Logisim project cache.circ as structural Verilog: 1 circuit, main circuit cache
module cache (
  input  [13:0] address,
  input  reset,
  input  clock,
  input  write,
  input  [31:0] data_in,
  output [31:0] data_out,
  output hit,
  output miss,
  output valid_miss,
  output [31:0] w0_out,
  output [31:0] w1_out,
  output [13:0] address_out,
  output [31:0] w2_out,
  output [31:0] w3_out
);

  wire and_1_out, and_2_out, and_3_out, and_4_out, multiplexer_4_out, not_1_out, s0hit, s1hit, s2hit, s3hit,
       set0, set1, set2, set3, valid0, valid1, valid2, valid3;
  wire [11:0] add0, add1, add2, add3;
  wire [31:0] data0, data1, data2, data3, s0w0, s0w1, s0w2, s0w3, s1w0, s1w1, s1w2, s1w3, s2w0, s2w1, s2w2,
       s2w3, s3w0, s3w1, s3w2, s3w3;

  Decoder #(.enable("false"), .select(2)) decoder_1 (
    .out0(set0), .out1(set1), .out2(set2), .out3(set3), .sel(address[3:2]));
  Multiplexer #(.select(2), .width(32)) multiplexer_1 (
    .in0(data0), .in1(data1), .in2(data2), .in3(data3), .out(data_out), .sel(address[3:2]));
  and and_1 (and_1_out, set0, clock);
  and and_2 (and_2_out, set1, clock);
  and and_3 (and_3_out, set2, clock);
  and and_4 (and_4_out, set3, clock);
  or or_1 (hit, s0hit, s1hit, s2hit, s3hit);
  Multiplexer #(.select(2), .width(32)) multiplexer_2 (
    .in0(s0w0), .in1(s1w0), .in2(s2w0), .in3(s3w0), .out(w0_out), .sel(address[3:2]));
  Multiplexer #(.select(2), .width(32)) multiplexer_3 (
    .in0(s0w2), .in1(s1w2), .in2(s2w2), .in3(s3w2), .out(w2_out), .sel(address[3:2]));
  not not_1 (not_1_out, hit);
  and and_5 (miss, not_1_out, ~reset);  // AND_Gate
  set set_1 (
    .reset(reset), .clock(and_1_out), .data_in(data_in), .word(address[1:0]), .write(write),
    .address(address[13:2]), .data_out(data0), .w0(s0w0), .w1(s0w1), .w2(s0w2), .w3(s0w3), .hit(s0hit),
    .address_out(add0), .valid_miss(valid0));  // open: miss
  set set_2 (
    .reset(reset), .clock(and_2_out), .data_in(data_in), .word(address[1:0]), .write(write),
    .address(address[13:2]), .data_out(data1), .w0(s1w0), .w1(s1w1), .w2(s1w2), .w3(s1w3), .hit(s1hit),
    .address_out(add1), .valid_miss(valid1));  // open: miss
  set set_3 (
    .reset(reset), .clock(and_3_out), .data_in(data_in), .word(address[1:0]), .write(write),
    .address(address[13:2]), .data_out(data2), .w0(s2w0), .w1(s2w1), .w2(s2w2), .w3(s2w3), .hit(s2hit),
    .address_out(add2), .valid_miss(valid2));  // open: miss
  set set_4 (
    .reset(reset), .clock(and_4_out), .data_in(data_in), .word(address[1:0]), .write(write),
    .address(address[13:2]), .data_out(data3), .w0(s3w0), .w1(s3w1), .w2(s3w2), .w3(s3w3), .hit(s3hit),
    .address_out(add3), .valid_miss(valid3));  // open: miss
  Multiplexer #(.select(2)) multiplexer_4 (
    .in0(valid0), .in1(valid1), .in2(valid2), .in3(valid3), .out(multiplexer_4_out), .sel(address[3:2]));
  Multiplexer #(.select(2), .width(32)) multiplexer_5 (
    .in0(s0w1), .in1(s1w1), .in2(s2w1), .in3(s3w1), .out(w1_out), .sel(address[3:2]));
  Multiplexer #(.select(2), .width(32)) multiplexer_6 (
    .in0(s0w3), .in1(s1w3), .in2(s2w3), .in3(s3w3), .out(w3_out), .sel(address[3:2]));
  and and_6 (valid_miss, multiplexer_4_out, miss);
  Multiplexer #(.select(2), .width(14)) multiplexer_7 (
    .in0({add0, 2'b00}), .in1({add1, 2'b01}), .in2({add2, 2'b10}), .in3({add3, 2'b11}), .out(address_out),
    .sel(address[3:2]));

  // Other names for the same wires on the sheet: word[1:0] = address[1:0]; data[31:0] = data_in;
  //   select_block[2:0] = address[4:2]; set_select[1:0] = address[3:2]; tag[11:0] = address[13:2];
  //   select_c[8:0] = address[13:5]
endmodule
