// Logisim project cpu.circ as structural Verilog: 1 circuit, main circuit cpu
module cpu (
  input  in_1,
  input  in_2,
  input  [3:0] in_3,
  input  [31:0] in_4,
  input  in_5,
  input  in_6
);

  wire ALUOpValid, ALUSrc, ALUSrc_EX, and_3_out, and_4_out, and_5_out, and_9_out, and_10_out, and_11_out,
       Branch, Branch_MEM, BranchFlush, BranchRes, BufferR, cacheClk, cacheWrite, clk, comparator_1_eq,
       comparator_2_eq, CPUclk, En1, En2, ex_mem_1_n_jal, ex_mem_1_n_memtoreg, ex_mem_1_n_regwrite,
       id_ex_1_n_branch, id_ex_1_n_jal, id_ex_1_n_memtoreg, id_ex_1_n_regwrite, is_op, JAL, JAL_WB, Jump,
       JumpReg, LB, MemToReg, MemToReg_WB, memWrite, miss, multiplexer_3_out, multiplexer_5_out,
       multiplexer_8_out, not_1_out, not_2_out, not_3_out, not_4_out, not_5_out, not_6_out, not_7_out,
       not_8_out, not_9_out, not_10_out, not_11_out, not_12_out, not_13_out, not_14_out, not_15_out,
       not_16_out, or_1_out, or_2_out, or_3_out, or_4_out, or_7_out, pipelineflush_1_loadflush,
       pipelineflush_1_rawflush, Prediction, RAW, RegDes, RegDes_EX, RegWrite, RegWrite_WB, SLTi, syscall,
       validMiss, zero, zero_MEM;
  wire [3:0] counter_1_q, counter_2_q, id_ex_1_n_memmask, MemMask, MemMask_MEM, memtocache_1_memmask;
  wire [4:0] ex_mem_1_n_write, instr1_EX, instr2, instr2_EX, instr3, multiplexer_6_out, multiplexer_12_out,
       sh_amount_EX, Write, Write_WB;
  wire [5:0] ALUOp, ALUOp_EX, func, func_EX, opcd_fnc, opcode_EX;
  wire [13:0] cache_1_p11;
  wire [15:2] MemAddr;
  wire [15:6] instr0;
  wire [31:0] added_PC, added_PC_MEM, Data_WB, ex_mem_1_n_pc, extended, extended_EX, final_writeData,
       id_ex_1_n_rd2, instr, MemData, memData_t, memtocache_1_word, memWriteData, multiplexer_1_out,
       multiplexer_7_out, multiplexer_9_out, multiplexer_11_out, new_PC, PC, PC_EX, PC_ID, PC_IF, PC_WB,
       rdData1, rdData1_EX, rdData2, rdData2_EX, rdData2_MEM, result, result_MEM, result_WB, shifter_1_out,
       W0, w0_t, W1, w1_t, W2, w2_t, W3, w3_t, writeData;
  wire [31:26] instr_ID;

  not not_1 (not_1_out, syscall);
  Multiplexer #(.width(32)) multiplexer_1 (.in0(new_PC), .in1(PC), .out(multiplexer_1_out), .sel(RAW));
  Register #(.width(32)) register_1 (.D(multiplexer_1_out), .en(not_1_out), .clk(CPUclk), .Q(PC), .clr(in_2));
  not not_2 (not_2_out, validMiss);
  Adder #(.width(32)) adder_1 (.a(PC), .b(32'h4), .out(PC_IF), .cin(1'b0));  // open: cout
  Clock clock_1 (.out(clk));
  and and_1 (En1, miss, validMiss);
  and and_2 (En2, miss, not_2_out);
  Counter #(.max('hf), .width(4)) counter_1 (
    .load(comparator_2_eq), .D(4'b0000), .count(En2), .Q(counter_1_q), .up(1'b1), .clk(clk));  // open: carry, clr
  Counter #(.max('hf), .width(4)) counter_2 (
    .D(4'b0000), .count(En1), .Q(counter_2_q), .up(1'b1), .clk(clk), .clr(comparator_1_eq));  // open: load, carry
  not not_3 (not_3_out, counter_2_q[1]);
  Comparator #(.width(4)) comparator_1 (.a(counter_2_q), .b(4'b1101), .eq(comparator_1_eq));  // open: gt, lt
  Comparator #(.width(4)) comparator_2 (.a(counter_1_q), .b(4'b1000), .eq(comparator_2_eq));  // open: gt, lt
  not not_4 (not_4_out, counter_1_q[0]);
  not not_5 (not_5_out, counter_1_q[1]);
  not not_6 (not_6_out, counter_1_q[2]);
  or or_1 (or_1_out, BufferR, in_5);
  // mem mem_1: pin names not known; wires that end beside it: PC, in_3, in_4, CPUclk, instr
  and and_3 (and_3_out, not_4_out, not_5_out, clk, not_6_out, counter_1_q[3]);
  and and_4 (and_4_out, counter_2_q[0], not_3_out, counter_2_q[2], counter_2_q[3], clk);
  Multiplexer #(.width(32)) multiplexer_2 (
    .in0(writeData), .in1({rdData2[31:8], writeData[7:0]}), .out(final_writeData), .sel(LB));
  IF_ID if_id_1 (
    .clk(CPUclk), .PC(PC_IF), .instr(instr), .reset(or_1_out), .n_PC(PC_ID),
    .n_instr({instr_ID, instr3, instr2, instr0, func}));
  Multiplexer multiplexer_3 (.in0(and_3_out), .in1(and_4_out), .out(multiplexer_3_out), .sel(validMiss));
  Shifter #(.width(32)) shifter_1 (.in(extended_EX), .\dist (5'b00010), .out(shifter_1_out));
  Multiplexer #(.width(5)) multiplexer_4 (.in0(instr2_EX), .in1(instr1_EX), .out(Write), .sel(RegDes_EX));
  Multiplexer multiplexer_5 (.in0(clk), .in1(multiplexer_3_out), .out(multiplexer_5_out), .sel(miss));
  Adder #(.width(32)) adder_2 (.a(PC_EX), .b(shifter_1_out), .out(added_PC), .cin(1'b0));  // open: cout
  Multiplexer #(.width(5)) multiplexer_6 (.in0(Write_WB), .in1({5{1'b1}}), .out(multiplexer_6_out), .sel(JAL_WB));
  Multiplexer #(.width(32)) multiplexer_7 (.in0(final_writeData), .in1(PC_WB), .out(multiplexer_7_out), .sel(JAL_WB));
  Multiplexer multiplexer_8 (.in0(multiplexer_5_out), .in1(clk), .out(multiplexer_8_out), .sel(in_6));
  Multiplexer #(.width(32)) multiplexer_9 (.in0(PC_IF), .in1(added_PC_MEM), .out(multiplexer_9_out), .sel(and_5_out));
  and and_5 (and_5_out, zero_MEM, Branch_MEM);
  Multiplexer #(.width(32)) multiplexer_10 (
    .in0(multiplexer_9_out), .in1({PC_ID[31:28], instr3, instr2, instr0, func, 2'b00}), .out(new_PC),
    .sel(Jump));
  and and_6 (CPUclk, multiplexer_8_out, not_7_out);
  not not_7 (not_7_out, syscall);
  SignExtend signextend_1 (.inpt({instr0, func}), .opcode(instr_ID), .outpt(extended));
  or or_2 (or_2_out, BufferR, in_5);
  // regfile RegisterFile: pin names not known; wires that end beside it: instr3, instr2, multiplexer_7_out, RegWrite_WB, CPUclk, multiplexer_6_out, rdData1, rdData2
  ID_EX id_ex_1 (
    .clk(CPUclk), .PC(PC_ID), .RD1(rdData1), .RD2(rdData2), .Ext(extended), .instr1(instr0[15:11]),
    .instr2(instr2), .RegDes(RegDes), .AluSrc(ALUSrc), .AluOp(ALUOp), .Branch(Branch), .MemMask(MemMask),
    .MemToReg(MemToReg), .JAL(JAL), .RegWrite(RegWrite), .func(func), .sh_amount(instr0[10:6]),
    .opcode(instr_ID), .reset(or_2_out), .n_PC(PC_EX), .n_RD1(rdData1_EX), .n_RD2(id_ex_1_n_rd2),
    .n_Ext(extended_EX), .n_instr1(instr1_EX), .n_instr2(instr2_EX), .n_RegDes(RegDes_EX),
    .n_AluSrc(ALUSrc_EX), .n_AluOp(ALUOp_EX), .n_Branch(id_ex_1_n_branch), .n_MemMask(id_ex_1_n_memmask),
    .n_MemToReg(id_ex_1_n_memtoreg), .n_JAL(id_ex_1_n_jal), .n_RegWrite(id_ex_1_n_regwrite),
    .n_sh_amount(sh_amount_EX), .n_func(func_EX), .n_opcode(opcode_EX));
  Multiplexer #(.width(32)) multiplexer_11 (
    .in0(rdData2_EX), .in1(extended_EX), .out(multiplexer_11_out), .sel(ALUSrc_EX));
  Multiplexer #(.width(5)) multiplexer_12 (.in0(instr0[15:11]), .in1(instr2), .out(multiplexer_12_out), .sel(RegDes));
  and and_7 (BranchRes, zero_MEM, Branch_MEM);
  ControlUnit controlunit_1 (
    .Opcode(instr_ID), .Func(func), .ALUSrc(ALUSrc), .RegWrite(RegWrite), .ALUOp(ALUOp),
    .ALUOpValid(ALUOpValid), .MemMask(MemMask), .JAL(JAL), .JumpReg(JumpReg), .RegDest(RegDes), .Jump(Jump),
    .Branch(Branch), .LB(LB), .MemToReg(MemToReg), .Syscall(syscall), .SLTi(SLTi));
  aluControl alucontrol_1 (.func(func_EX), .aluOP(ALUOp_EX), .opcd_fnc(opcd_fnc), .is_op(is_op));
  or or_3 (or_3_out, BufferR, in_5);
  alu alu_1 (
    .rs(rdData1_EX), .rt_imm(multiplexer_11_out), .opcd_fnc(opcd_fnc), .shft_amt(sh_amount_EX), .is_i(is_op),
    .result(result), .zero(zero));
  PipelineFlush pipelineflush_1 (
    .WriteReg(multiplexer_12_out), .ReadRegI(instr3), .ReadRegII(instr2), .Branch(Branch),
    .BranchPrediction(Prediction), .BranchResult(BranchRes), .clk(clk), .MemToReg(MemToReg),
    .RAWFlush(pipelineflush_1_rawflush), .BranchFlush(BranchFlush), .LoadFlush(pipelineflush_1_loadflush));
  EX_MEM ex_mem_1 (
    .clk(CPUclk), .PC(PC_EX), .Result(result), .RD2(id_ex_1_n_rd2), .Write(Write), .Zero(zero),
    .Branch(id_ex_1_n_branch), .MemMask(id_ex_1_n_memmask), .MemToReg(id_ex_1_n_memtoreg),
    .JAL(id_ex_1_n_jal), .RegWrite(id_ex_1_n_regwrite), .added_PC(added_PC), .n_Result(result_MEM),
    .n_PC(ex_mem_1_n_pc), .n_RD2(rdData2_MEM), .n_Write(ex_mem_1_n_write), .n_Zero(zero_MEM),
    .n_Branch(Branch_MEM), .n_MemMask(MemMask_MEM), .n_MemToReg(ex_mem_1_n_memtoreg), .n_JAL(ex_mem_1_n_jal),
    .n_RegWrite(ex_mem_1_n_regwrite), .n_added_PC(added_PC_MEM));
  and and_8 (RAW, pipelineflush_1_rawflush, pipelineflush_1_loadflush);
  Multiplexer #(.width(32)) multiplexer_13 (.in0(result_WB), .in1(Data_WB), .out(writeData), .sel(MemToReg_WB));
  not not_8 (not_8_out, MemMask_MEM[0]);
  not not_9 (not_9_out, MemMask_MEM[1]);
  not not_10 (not_10_out, MemMask_MEM[2]);
  or or_4 (or_4_out, BufferR, in_5);
  and and_9 (and_9_out, not_8_out, not_9_out, not_10_out, MemMask_MEM[3]);
  Multiplexer #(.width(32)) multiplexer_14 (
    .in0(rdData2_MEM), .in1({MemData[31:8], rdData2_MEM[7:0]}), .out(memWriteData), .sel(and_9_out));
  MEM_WB mem_wb_1 (
    .clk(CPUclk), .PC(ex_mem_1_n_pc), .Result(result_MEM), .Data(MemData), .Write(ex_mem_1_n_write),
    .MemToReg(ex_mem_1_n_memtoreg), .JAL(ex_mem_1_n_jal), .RegWrite(ex_mem_1_n_regwrite), .reset(or_4_out),
    .n_Result(result_WB), .n_PC(PC_WB), .n_Data(Data_WB), .n_Write(Write_WB), .n_MemToReg(MemToReg_WB),
    .n_JAL(JAL_WB), .n_RegWrite(RegWrite_WB));
  Multiplexer #(.width(32)) multiplexer_15 (.in0(w0_t), .in1(memData_t), .out(W0), .sel(not_11_out));
  Multiplexer #(.width(32)) multiplexer_16 (.in0(w1_t), .in1(memData_t), .out(W1), .sel(not_11_out));
  Multiplexer #(.width(32)) multiplexer_17 (.in0(w2_t), .in1(memData_t), .out(W2), .sel(not_11_out));
  Multiplexer #(.width(32)) multiplexer_18 (.in0(w3_t), .in1(memData_t), .out(W3), .sel(not_11_out));
  // cache cache_1: pin names not known; wires that end beside it: result_MEM[15:2], in_1, clk, cacheWrite, memWriteData, MemData, validMiss, miss, w0_t, w1_t, cache_1_p11, w2_t, w3_t
  or or_5 (BufferR, RAW, BranchFlush);
  not not_11 (not_11_out, memWrite);
  memToCache memtocache_1 (
    .miss(miss), .validmiss(validMiss), .word_0(W0), .word_1(W1), .word_2(W2), .word_3(W3),
    .address_out(cache_1_p11), .clk(clk), .memmask(memtocache_1_memmask), .memwrite(memWrite),
    .word(memtocache_1_word), .address(MemAddr));
  // memDelayed memdelayed_1: pin names not known; wires that end beside it: {{16{1'b0}}, MemAddr, 2'b00}, memtocache_1_memmask, memtocache_1_word, clk, memData_t
  not not_12 (not_12_out, instr_ID[28]);
  not not_13 (not_13_out, instr_ID[30]);
  not not_14 (not_14_out, instr_ID[28]);
  not not_15 (not_15_out, instr_ID[29]);
  not not_16 (not_16_out, instr_ID[30]);
  and and_10 (and_10_out, instr_ID[26], instr_ID[27], not_12_out, instr_ID[29], not_13_out, instr_ID[31]);
  SaturatingCounter_2bit saturatingcounter_2bit_1 (
    .request(Branch), .result(Branch_MEM), .teken(BranchRes), .clk(CPUclk), .prediction(Prediction));
  and and_11 (and_11_out, instr_ID[26], instr_ID[27], not_14_out, not_15_out, not_16_out, instr_ID[31]);
  or or_6 (cacheWrite, and_10_out, memWrite);
  or or_7 (or_7_out, and_10_out, and_11_out);
  and and_12 (cacheClk, or_7_out, clk);

  // Other names for the same wires on the sheet: instr0[5:0] = func; instr_ID[25:0] = {instr3, instr2, instr0, func};
  //   Jinstr[25:0] = {instr3, instr2, instr0, func}; sh_amount[4:0] = instr0[10:6]; instr1[4:0] = instr0[15:11];
  //   opcode[5:0] = instr_ID; MemToCacheAddr[13:0] = MemAddr; Re = in_5
endmodule
