// Logisim project memToCache.circ as structural Verilog: 1 circuit, main circuit memToCache
module memToCache (
  input  miss,
  input  validmiss,
  input  [31:0] word_0,
  input  [31:0] word_1,
  input  [31:0] word_2,
  input  [31:0] word_3,
  input  [13:0] address_out,
  input  clk,
  output [3:0] memmask,
  output memwrite,
  output [31:0] word,
  output [13:0] address
);

  wire and_1_out, miss_t, not_1_out, not_2_out, t_ff_1_q;

  and and_1 (and_1_out, address[0], address[1]);
  and and_2 (miss_t, miss, validmiss);
  T_Flip_Flop t_ff_1 (.T(miss_t), .clk(and_1_out), .Q(t_ff_1_q), .reset(not_1_out));  // open: Qn, preset
  not not_1 (not_1_out, miss_t);
  D_Flip_Flop d_ff_1 (.D(not_2_out), .clk(clk), .Q(memmask[3]));  // open: Qn, preset, reset
  not not_2 (not_2_out, t_ff_1_q);
  Multiplexer #(.select(2), .width(32), .enable("false")) multiplexer_1 (
    .in0(word_0), .in1(word_1), .in2(word_2), .in3(word_3), .out(word), .sel(address[1:0]));
  MemAddressGen memaddressgen_1 (
    .address(address_out), .miss(miss_t), .clk(clk), .read(miss_t), .memaddress(address));  // open: memmask, readmem

  assign memmask[2:0] = {3{memmask[3]}};
  assign memwrite = memmask[3];

  // Other names for the same wires on the sheet: bit0 = address[0]; bit1 = address[1]
endmodule
