// Logisim project set.circ as structural Verilog: 1 circuit, main circuit set
module set (
  input  reset,
  input  clock,
  input  [31:0] data_in,
  input  [1:0] word,
  input  write,
  input  [11:0] address,
  output [31:0] data_out,
  output [31:0] w0,
  output [31:0] w1,
  output [31:0] w2,
  output [31:0] w3,
  output hit,
  output [11:0] address_out,
  output valid_miss,
  output miss
);

  wire a0, a1, a2, a3, a4, a5, a6, a7, and_1_out, and_2_out, and_3_out, and_4_out, and_5_out, and_6_out,
       and_9_out, and_10_out, and_11_out, and_12_out, and_13_out, and_14_out, and_15_out, and_16_out,
       and_17_out, and_18_out, and_19_out, and_20_out, b, comparator_1_eq, comparator_2_eq, not_2_out,
       or_4_out, s0, s1;
  wire [1:0] not_1_out, subtractor_1_out, vc0, vc1;
  wire [1:1] or_1_out;
  wire [11:0] tag0, tag1;
  wire [31:0] data0, data1, data2, data3, data4, data5, data6, data7;

  Decoder #(.enable("false"), .select(3)) decoder_1 (
    .out0(a0), .out1(a1), .out2(a2), .out3(a3), .out4(a4), .out5(a5), .out6(a6), .out7(a7), .sel({b, word}));
  or or_1 (or_1_out[1], vc0[1], ~b);  // OR_Gate
  not not_1 (not_1_out[0], b);
  or or_2 (not_1_out[1], vc1[1], b);
  Register #(.width(2)) register_1 (.D({or_1_out[1], b}), .en(1'b1), .clk(and_1_out), .Q(vc0), .clr(reset));
  and and_1 (and_1_out, write, clock);
  and and_2 (and_2_out, write, clock);
  Register #(.width(2)) register_2 (.D(not_1_out), .en(1'b1), .clk(and_2_out), .Q(vc1), .clr(reset));
  Subtractor #(.width(2)) subtractor_1 (.a({s1, s0}), .b(2'b01), .out(subtractor_1_out));  // open: bin, bout
  not not_2 (not_2_out, b);
  Multiplexer #(.select(3), .width(32)) multiplexer_1 (
    .in0(data0), .in1(data1), .in2(data2), .in3(data3), .in4(data4), .in5(data5), .in6(data6), .in7(data7),
    .out(data_out), .sel({subtractor_1_out[0], word}));
  Register #(.width(12)) register_3 (.D(address), .en(not_2_out), .clk(and_3_out), .Q(tag0), .clr(reset));
  and and_3 (and_3_out, write, clock);
  Register #(.width(12)) register_4 (.D(address), .en(b), .clk(and_4_out), .Q(tag1), .clr(reset));
  and and_4 (and_4_out, write, clock);
  or or_3 (hit, s0, s1);
  not not_3 (miss, hit);
  and and_5 (and_5_out, ~vc0[0], vc0[1]);  // AND_Gate
  and and_6 (and_6_out, vc0[1], ~vc1[1]);  // AND_Gate
  Comparator #(.width(12)) comparator_1 (.a(address), .b(tag0), .eq(comparator_1_eq));  // open: gt, lt
  and and_7 (s1, vc1[1], comparator_2_eq);
  Comparator #(.width(12)) comparator_2 (.a(address), .b(tag1), .eq(comparator_2_eq));  // open: gt, lt
  or or_4 (or_4_out, and_5_out, and_6_out);
  and and_8 (s0, vc0[1], comparator_1_eq);
  and and_9 (and_9_out, miss, or_4_out);
  and and_10 (and_10_out, hit, s1);
  Register #(.width(32)) register_5 (.D(data_in), .en(a0), .clk(and_11_out), .Q(data0), .clr(reset));
  and and_11 (and_11_out, clock, write);
  Register #(.width(32)) register_6 (.D(data_in), .en(a4), .clk(and_12_out), .Q(data4), .clr(reset));
  and and_12 (and_12_out, clock, write);
  or or_5 (b, and_9_out, and_10_out);
  Multiplexer #(.width(32)) multiplexer_2 (.in0(data0), .in1(data4), .out(w0), .sel(b));
  Register #(.width(32)) register_7 (.D(data_in), .en(a1), .clk(and_13_out), .Q(data1), .clr(reset));
  and and_13 (and_13_out, clock, write);
  Register #(.width(32)) register_8 (.D(data_in), .en(a5), .clk(and_14_out), .Q(data5), .clr(reset));
  and and_14 (and_14_out, clock, write);
  and and_15 (and_15_out, vc0[1], ~b);  // AND_Gate
  and and_16 (and_16_out, b, vc1[1]);
  or or_6 (valid_miss, and_15_out, and_16_out);
  Register #(.width(32)) register_9 (.D(data_in), .en(a2), .clk(and_17_out), .Q(data2), .clr(reset));
  and and_17 (and_17_out, clock, write);
  Register #(.width(32)) register_10 (.D(data_in), .en(a6), .clk(and_18_out), .Q(data6), .clr(reset));
  and and_18 (and_18_out, clock, write);
  Multiplexer #(.width(32)) multiplexer_3 (.in0(data1), .in1(data5), .out(w1), .sel(b));
  Multiplexer #(.width(12)) multiplexer_4 (.in0(tag0), .in1(tag1), .out(address_out), .sel(b));
  Register #(.width(32)) register_11 (.D(data_in), .en(a3), .clk(and_19_out), .Q(data3), .clr(reset));
  and and_19 (and_19_out, clock, write);
  Register #(.width(32)) register_12 (.D(data_in), .en(a7), .clk(and_20_out), .Q(data7), .clr(reset));
  and and_20 (and_20_out, clock, write);
  Multiplexer #(.width(32)) multiplexer_5 (.in0(data2), .in1(data6), .out(w2), .sel(b));
  Multiplexer #(.width(32)) multiplexer_6 (.in0(data3), .in1(data7), .out(w3), .sel(b));
endmodule
