// Logisim project sign_extend.circ as structural Verilog: 1 circuit, main circuit SignExtend
module SignExtend (
  input  [15:0] inpt,
  input  [5:0] opcode,
  output [31:0] outpt
);

  wire and_2_out, and_3_out, and_4_out, not_1_out, not_2_out, not_3_out, not_4_out, not_5_out, not_6_out,
       not_7_out, not_8_out, not_9_out, or_1_out, or_2_out;
  wire [31:31] and_1_out;

  not not_1 (not_1_out, opcode[0]);
  and and_1 (and_1_out[31], opcode[0], not_1_out);
  Multiplexer #(.width(32), .enable("false")) multiplexer_1 (
    .in0({{17{inpt[15]}}, inpt[14:0]}), .in1({{16{and_1_out[31]}}, inpt}), .out(outpt), .sel(or_1_out));
  or or_1 (or_1_out, and_2_out, and_3_out);
  and and_2 (and_2_out, opcode[0], not_2_out, not_3_out, opcode[3], not_4_out, not_5_out);
  and and_3 (and_3_out, not_6_out, not_7_out, opcode[3], opcode[2], or_2_out);
  not not_2 (not_2_out, opcode[1]);
  not not_3 (not_3_out, opcode[2]);
  not not_4 (not_4_out, opcode[4]);
  not not_5 (not_5_out, opcode[5]);
  not not_6 (not_6_out, opcode[5]);
  or or_2 (or_2_out, not_8_out, and_4_out);
  not not_7 (not_7_out, opcode[4]);
  and and_4 (and_4_out, not_9_out, opcode[0]);
  not not_8 (not_8_out, opcode[0]);
  not not_9 (not_9_out, opcode[1]);

  // Other names for the same wires on the sheet: op5 = opcode[0]; op4 = opcode[1]; op3 = opcode[2]; op2 = opcode[3];
  //   op1 = opcode[4]; op0 = opcode[5]

  // Notes on the sheet:
  //   16 bit input
  //   32-bit output
endmodule
